# Fritzing sketch conexion_node (saved by Fritzing 0.9.2b)
breadboards: 1

parts:
  U1 = NodeMCU V1.0
  S1 = H-Bridge with L298N
  M1 = DC Motor
  M2 = DC Motor

nets:
  N1: U1.D1, U1.D2, S1.IN1, S1.IN2
  N2: U1.D3, S1.IN3
  N3: U1.D4, S1.IN4
  N4: U1.D5, S1.ENA
  N5: U1.D6, S1.ENB
  N6: S1.M1-01, M1.pin_2
  N7: S1.M1-02, M1.pin_1
  N8: S1.M2-01, M2.pin_2
  N9: S1.M2-02, M2.pin_1

custom parts:
  NodeMCU V1.0: ESP8266 based NodeMCU
  H-Bridge with L298N: h-bridge
